// Logisim project 04062018lab.circ as structural Verilog: 1 circuit, main circuit main
module main (
  input  in_1,
  input  in_2,
  input  in_3,
  input  in_4,
  input  in_5,
  input  in_6,
  input  in_7,
  input  in_8,
  input  _1,
  input  _2,
  input  _4,
  input  _8,
  input  in_13,
  input  in_14,
  input  _1_2,
  input  _2_2,
  input  _4_2,
  input  _8_2,
  input  in_19,
  input  MREQ,
  input  IORQ,
  input  WR,
  input  RD,
  output out_24,
  output out_25,
  output out_26,
  output out_27,
  output out_28,
  output out_29,
  output out_30,
  output out_31,
  output out_32,
  output out_33,
  output out_34,
  output out_35,
  output out_36,
  output out_37,
  output out_38,
  output out_39,
  output out_40,
  output out_41,
  output out_42,
  output out_43,
  output MWR,
  output out_45,
  output out_46,
  output out_47
);

  wire and_1_out, and_2_out, and_3_out, and_4_out, and_5_out, and_6_out, and_7_out, and_8_out, nor_1_out,
       not_1_out, not_2_out, not_3_out, not_4_out, not_5_out, not_6_out, not_7_out, not_8_out, t_ff_1_q,
       t_ff_2_q, t_ff_3_q, t_ff_4_qn, t_ff_5_q, t_ff_6_qn, t_ff_7_q, t_ff_8_q, t_ff_9_qn, t_ff_10_q,
       t_ff_11_qn, t_ff_12_q, t_ff_13_q, t_ff_14_q, xor_1_out, xor_2_out, xor_3_out, xor_4_out;

  T_Flip_Flop t_ff_1 (.T(in_1), .clk(in_2), .Q(t_ff_1_q), .reset(nor_1_out));  // open: Qn, preset
  not not_1 (not_1_out, _1_2);
  not not_2 (not_2_out, _2_2);
  not not_3 (not_3_out, _4_2);
  not not_4 (not_4_out, _8_2);
  T_Flip_Flop t_ff_2 (.T(in_1), .clk(t_ff_1_q), .Q(t_ff_2_q), .reset(nor_1_out));  // open: Qn, preset
  T_Flip_Flop t_ff_3 (.T(in_7), .clk(in_8), .Q(t_ff_3_q), .reset(and_1_out));  // open: Qn, preset
  and and_1 (and_1_out, not_5_out, t_ff_14_q);
  not not_5 (not_5_out, _1);
  not not_6 (not_6_out, _2);
  not not_7 (not_7_out, _4);
  not not_8 (not_8_out, _8);
  T_Flip_Flop t_ff_4 (.T(in_13), .clk(in_14), .Qn(t_ff_4_qn), .reset(and_2_out));  // open: Q, preset
  and and_2 (and_2_out, not_1_out, t_ff_13_q);
  Counter #(.width(4), .max('h9), .trigger("falling")) counter_1 (
    .clk(in_19), .Q({out_38, out_32, out_27, out_24}));  // open: clr, load, up, count, D, carry
  xor xor_1 (xor_1_out, t_ff_1_q, in_3);
  T_Flip_Flop t_ff_5 (.T(in_7), .clk(t_ff_3_q), .Q(t_ff_5_q), .reset(and_3_out));  // open: Qn, preset
  and and_3 (and_3_out, not_6_out, t_ff_14_q);
  T_Flip_Flop #(.trigger("falling")) t_ff_6 (
    .T(in_13), .clk(t_ff_4_qn), .Qn(t_ff_6_qn), .reset(and_4_out));  // open: Q, preset
  and and_4 (and_4_out, not_2_out, t_ff_13_q);
  T_Flip_Flop t_ff_7 (.T(in_1), .clk(t_ff_2_q), .Q(t_ff_7_q), .reset(nor_1_out));  // open: Qn, preset
  xor xor_2 (xor_2_out, t_ff_2_q, in_4);
  T_Flip_Flop t_ff_8 (.T(in_7), .clk(t_ff_5_q), .Q(t_ff_8_q), .reset(and_6_out));  // open: Qn, preset
  T_Flip_Flop #(.trigger("falling")) t_ff_9 (
    .T(in_13), .clk(t_ff_6_qn), .Qn(t_ff_9_qn), .reset(and_5_out));  // open: Q, preset
  and and_5 (and_5_out, not_3_out, t_ff_13_q);
  or or_1 (MWR, MREQ, WR);
  // OR_Gate or_2 has open pins: out=out_45
  // OR_Gate or_3 has open pins: out=out_46
  // OR_Gate or_4 has open pins: out=out_47
  T_Flip_Flop t_ff_10 (.T(in_1), .clk(t_ff_7_q), .Q(t_ff_10_q), .reset(nor_1_out));  // open: Qn, preset
  and and_6 (and_6_out, not_7_out, t_ff_14_q);
  T_Flip_Flop #(.trigger("falling")) t_ff_11 (
    .T(in_13), .clk(t_ff_9_qn), .Qn(t_ff_11_qn), .reset(and_7_out));  // open: Q, preset
  and and_7 (and_7_out, not_4_out, t_ff_13_q);
  xor xor_3 (xor_3_out, t_ff_7_q, in_5);
  T_Flip_Flop t_ff_12 (.T(in_7), .clk(t_ff_8_q), .Q(t_ff_12_q), .reset(and_8_out));  // open: Qn, preset
  and and_8 (and_8_out, not_8_out, t_ff_14_q);
  T_Flip_Flop #(.trigger("falling")) t_ff_13 (
    .T(in_13), .clk(t_ff_11_qn), .Q(t_ff_13_q), .reset(t_ff_13_q));  // open: Qn, preset
  Counter #(.width(3), .max('h6)) counter_2 (
    .clk(out_24), .Q({out_39, out_33, out_28}));  // open: clr, load, up, count, D, carry
  xor xor_4 (xor_4_out, t_ff_10_q, in_6);
  T_Flip_Flop t_ff_14 (.T(in_7), .clk(t_ff_12_q), .Q(t_ff_14_q), .reset(t_ff_14_q));  // open: Qn, preset
  nor nor_1 (nor_1_out, xor_4_out, xor_3_out, xor_2_out, xor_1_out);
  Counter #(.width(4), .max('h9), .trigger("falling")) counter_3 (
    .clk(out_28), .Q({out_40, out_34, out_29, out_25}));  // open: clr, load, up, count, D, carry
  Counter #(.width(3), .max('h7)) counter_4 (
    .clk(out_25), .Q({out_41, out_35, out_30}));  // open: clr, load, up, count, D, carry
  Counter #(.width(4), .max('h9), .trigger("falling")) counter_5 (
    .clk(out_30), .Q({out_42, out_36, out_31, out_26}));  // open: clr, load, up, count, D, carry
  Counter #(.width(2), .max('h2)) counter_6 (
    .clk(out_26), .Q({out_43, out_37}));  // open: clr, load, up, count, D, carry
  // AND_Gate and_9 is placed but not wired
  POR por_1 ();  // open: out

  // Notes on the sheet:
  //   Konwerter z Z80
  //   Zegarek binarny
endmodule
