// Logisim project 06062018.circ as structural Verilog: 1 circuit, main circuit main
module main (
  input  [3:0] in_1,
  input  [3:0] in_2,
  input  in_3,
  input  in_4
);

  wire and_1_out, clock_1_out, decoder_1_out0, decoder_1_out1, decoder_1_out2, decoder_1_out3,
       decoder_1_out4, decoder_1_out5, decoder_1_out6, decoder_1_out7, decoder_1_out8, decoder_1_out9,
       decoder_2_out0, decoder_2_out1, decoder_2_out2, decoder_2_out3, decoder_2_out4, decoder_2_out5,
       decoder_2_out6, decoder_2_out7, decoder_2_out8, decoder_3_out0, decoder_3_out1, decoder_3_out2,
       decoder_3_out3, decoder_3_out4, decoder_3_out5, decoder_3_out6, decoder_3_out7, decoder_3_out8,
       decoder_3_out9, decoder_4_out0, decoder_4_out1, decoder_4_out2, decoder_4_out3, decoder_4_out4,
       decoder_4_out5, decoder_4_out6, decoder_4_out7, decoder_4_out8, decoder_4_out9, nor_1_out, nor_2_out,
       nor_3_out, nor_4_out, nor_5_out, not_1_out, or_1_out, or_2_out, or_3_out, or_4_out, or_5_out,
       or_6_out, or_7_out, or_8_out, or_9_out, or_10_out, or_11_out, or_12_out, or_13_out, or_14_out,
       or_15_out, or_16_out, or_17_out, or_18_out, or_19_out, or_20_out, or_21_out, or_22_out;
  wire [2:0] counter_2_q;
  wire [3:0] counter_1_q;

  Clock clock_1 (.out(clock_1_out));
  Decoder #(.select(4)) decoder_1 (
    .out0(decoder_1_out0), .out1(decoder_1_out1), .out2(decoder_1_out2), .out3(decoder_1_out3),
    .out4(decoder_1_out4), .out5(decoder_1_out5), .out6(decoder_1_out6), .out7(decoder_1_out7),
    .out8(decoder_1_out8), .out9(decoder_1_out9), .sel(in_1));  // open: out10, out11, out12, out13, out14, out15, en
  Decoder #(.select(4)) decoder_2 (
    .out0(decoder_2_out0), .out1(decoder_2_out1), .out2(decoder_2_out2), .out3(decoder_2_out3),
    .out4(decoder_2_out4), .out5(decoder_2_out5), .out6(decoder_2_out6), .out7(decoder_2_out7),
    .out8(decoder_2_out8), .sel(in_2));  // open: out9, out10, out11, out12, out13, out14, out15, en
  Counter #(.width(4), .max('h9)) counter_1 (
    .clr(in_3), .clk(clock_1_out), .Q(counter_1_q));  // open: load, up, count, D, carry
  Decoder #(.select(4)) decoder_3 (
    .out0(decoder_3_out0), .out1(decoder_3_out1), .out2(decoder_3_out2), .out3(decoder_3_out3),
    .out4(decoder_3_out4), .out5(decoder_3_out5), .out6(decoder_3_out6), .out7(decoder_3_out7),
    .out8(decoder_3_out8), .out9(decoder_3_out9), .sel(counter_1_q));  // open: out10, out11, out12, out13, out14, out15, en
  or or_1 (or_1_out, decoder_1_out0, decoder_1_out2, decoder_1_out3, decoder_1_out5, decoder_1_out6, decoder_1_out7, decoder_1_out8, decoder_1_out9);
  or or_2 (or_2_out, decoder_1_out0, decoder_1_out1, decoder_1_out2, decoder_1_out3, decoder_1_out4, decoder_1_out7, decoder_1_out8, decoder_1_out9);
  or or_3 (or_3_out, decoder_1_out0, decoder_1_out1, decoder_1_out3, decoder_1_out4, decoder_1_out5, decoder_1_out6, decoder_1_out7, decoder_1_out8, decoder_1_out9);
  or or_4 (or_4_out, decoder_1_out0, decoder_1_out2, decoder_1_out3, decoder_1_out5, decoder_1_out6, decoder_1_out8, decoder_1_out9);
  or or_5 (or_5_out, decoder_1_out0, decoder_1_out2, decoder_1_out6, decoder_1_out8);
  or or_6 (or_6_out, decoder_1_out0, decoder_1_out4, decoder_1_out5, decoder_1_out6, decoder_1_out8, decoder_1_out9);
  or or_7 (or_7_out, decoder_1_out2, decoder_1_out3, decoder_1_out4, decoder_1_out5, decoder_1_out6, decoder_1_out8, decoder_1_out9);
  nor nor_1 (nor_1_out, decoder_2_out4, decoder_2_out5);
  nor nor_2 (nor_2_out, decoder_2_out6, decoder_2_out7);
  not not_1 (not_1_out, decoder_2_out2);
  nor nor_3 (nor_3_out, decoder_2_out1, decoder_2_out4, decoder_2_out7);
  or or_8 (or_8_out, decoder_2_out0, decoder_2_out2, decoder_2_out6, decoder_2_out8);
  nor nor_4 (nor_4_out, decoder_2_out1, decoder_2_out2, decoder_2_out3, decoder_2_out8);
  nor nor_5 (nor_5_out, decoder_2_out0, decoder_2_out1, decoder_2_out8);
  or or_9 (or_9_out, decoder_3_out0, decoder_3_out2, decoder_3_out6, decoder_3_out8);
  and and_1 (and_1_out, counter_1_q[0], counter_1_q[3]);
  or or_10 (or_10_out, decoder_3_out0, decoder_3_out2, decoder_3_out3, decoder_3_out5, decoder_3_out6, decoder_3_out7, decoder_3_out8, decoder_3_out9);
  or or_11 (or_11_out, decoder_3_out0, decoder_3_out1, decoder_3_out2, decoder_3_out3, decoder_3_out4, decoder_3_out7, decoder_3_out8, decoder_3_out9);
  or or_12 (or_12_out, decoder_3_out0, decoder_3_out1, decoder_3_out3, decoder_3_out4, decoder_3_out5, decoder_3_out6, decoder_3_out7, decoder_3_out8, decoder_3_out9);
  or or_13 (or_13_out, decoder_3_out0, decoder_3_out2, decoder_3_out3, decoder_3_out5, decoder_3_out6, decoder_3_out8, decoder_3_out9);
  or or_14 (or_14_out, decoder_3_out0, decoder_3_out4, decoder_3_out5, decoder_3_out6, decoder_3_out8, decoder_3_out9);
  or or_15 (or_15_out, decoder_3_out2, decoder_3_out3, decoder_3_out4, decoder_3_out5, decoder_3_out6, decoder_3_out8, decoder_3_out9);
  _7_Segment_Display u_7_segment_display_1 (
    .g(nor_5_out), .f(nor_4_out), .a(nor_1_out), .b(nor_2_out), .e(or_8_out), .d(nor_3_out), .c(not_1_out));  // open: dp
  Counter #(.width(3), .max('h7), .trigger("falling")) counter_2 (
    .clr(in_4), .clk(and_1_out), .Q(counter_2_q));  // open: load, up, count, D, carry
  _7_Segment_Display u_7_segment_display_2 (
    .g(or_15_out), .f(or_14_out), .a(or_10_out), .b(or_11_out), .e(or_9_out), .d(or_13_out), .c(or_12_out));  // open: dp
  Decoder #(.select(4)) decoder_4 (
    .out0(decoder_4_out0), .out1(decoder_4_out1), .out2(decoder_4_out2), .out3(decoder_4_out3),
    .out4(decoder_4_out4), .out5(decoder_4_out5), .out6(decoder_4_out6), .out7(decoder_4_out7),
    .out8(decoder_4_out8), .out9(decoder_4_out9), .sel({1'b0, counter_2_q}));  // open: out10, out11, out12, out13, out14, out15, en
  _7_Segment_Display u_7_segment_display_3 (
    .g(or_7_out), .f(or_6_out), .a(or_1_out), .b(or_2_out), .e(or_5_out), .d(or_4_out), .c(or_3_out));  // open: dp
  or or_16 (or_16_out, decoder_4_out0, decoder_4_out2, decoder_4_out3, decoder_4_out5, decoder_4_out6, decoder_4_out7, decoder_4_out8, decoder_4_out9);
  or or_17 (or_17_out, decoder_4_out0, decoder_4_out1, decoder_4_out2, decoder_4_out3, decoder_4_out4, decoder_4_out7, decoder_4_out8, decoder_4_out9);
  or or_18 (or_18_out, decoder_4_out0, decoder_4_out1, decoder_4_out3, decoder_4_out4, decoder_4_out5, decoder_4_out6, decoder_4_out7, decoder_4_out8, decoder_4_out9);
  or or_19 (or_19_out, decoder_4_out0, decoder_4_out2, decoder_4_out3, decoder_4_out5, decoder_4_out6, decoder_4_out8, decoder_4_out9);
  or or_20 (or_20_out, decoder_4_out0, decoder_4_out2, decoder_4_out6, decoder_4_out8);
  or or_21 (or_21_out, decoder_4_out0, decoder_4_out4, decoder_4_out5, decoder_4_out6, decoder_4_out8, decoder_4_out9);
  or or_22 (or_22_out, decoder_4_out2, decoder_4_out3, decoder_4_out4, decoder_4_out5, decoder_4_out6, decoder_4_out8, decoder_4_out9);
  _7_Segment_Display u_7_segment_display_4 (
    .g(or_22_out), .f(or_21_out), .a(or_16_out), .b(or_17_out), .e(or_20_out), .d(or_19_out), .c(or_18_out));  // open: dp

  // Notes on the sheet:
  //   OR
  //   NOR
  //   Zegarek
endmodule
