// Logisim project 11062018.circ as structural Verilog: 1 circuit, main circuit main
module main (
  input  [7:0] Data,
  input  IORQ,
  input  IOWR,
  input  ADDRS,
  input  ADDRD,
  input  in_6,
  input  in_7,
  input  [7:0] Data_2,
  input  IORQ_2,
  input  IOWR_2,
  input  ADDRS_2,
  input  ADDRD_2,
  input  in_13
);

  wire or_1_out, or_2_out, or_3_out, or_4_out;
  wire [7:0] controlled_buffer_1_out, controlled_buffer_2_out, controlled_buffer_3_out, register_1_q,
       register_2_q, register_3_q, register_4_q, register_5_q, register_6_q;

  or or_1 (or_1_out, IORQ, IOWR, ADDRS);
  or or_2 (or_2_out, IORQ, IOWR, ADDRD);
  Register #(.trigger("falling")) register_1 (
    .D(Data), .en(register_2_q[0]), .clk(or_1_out), .Q(register_1_q));  // open: clr
  or or_3 (or_3_out, IORQ_2, IOWR_2, ADDRS_2);
  or or_4 (or_4_out, IORQ_2, IOWR_2, ADDRD_2);
  Register #(.trigger("falling")) register_2 (.D(Data), .en(in_6), .clk(or_2_out), .Q(register_2_q));  // open: clr
  Register #(.trigger("falling")) register_3 (.D(Data_2), .en(in_7), .clk(or_3_out), .Q(register_3_q));  // open: clr
  Register #(.trigger("falling")) register_4 (.D(Data_2), .en(in_13), .clk(or_4_out), .Q(register_4_q));  // open: clr
  assign controlled_buffer_1_out = register_4_q[0] ? register_3_q : 8'bz;  // Controlled_Buffer controlled_buffer_1
  _7_Segment_Display u_7_segment_display_1 (
    .g(register_1_q[6]), .f(register_1_q[5]), .a(register_1_q[0]), .b(register_1_q[1]), .e(register_1_q[4]),
    .d(register_1_q[3]), .c(register_1_q[2]), .dp(register_1_q[7]));
  Register #(.trigger("falling")) register_5 (
    .D(Data), .en(register_2_q[1]), .clk(or_1_out), .Q(register_5_q));  // open: clr
  _7_Segment_Display u_7_segment_display_2 (
    .g(controlled_buffer_1_out[6]), .f(controlled_buffer_1_out[5]), .a(controlled_buffer_1_out[0]),
    .b(controlled_buffer_1_out[1]), .e(controlled_buffer_1_out[4]), .d(controlled_buffer_1_out[3]),
    .c(controlled_buffer_1_out[2]), .dp(controlled_buffer_1_out[7]));
  assign controlled_buffer_2_out = register_4_q[1] ? register_3_q : 8'bz;  // Controlled_Buffer controlled_buffer_2
  _7_Segment_Display u_7_segment_display_3 (
    .g(register_5_q[6]), .f(register_5_q[5]), .a(register_5_q[0]), .b(register_5_q[1]), .e(register_5_q[4]),
    .d(register_5_q[3]), .c(register_5_q[2]), .dp(register_5_q[7]));
  _7_Segment_Display u_7_segment_display_4 (
    .g(controlled_buffer_2_out[6]), .f(controlled_buffer_2_out[5]), .a(controlled_buffer_2_out[0]),
    .b(controlled_buffer_2_out[1]), .e(controlled_buffer_2_out[4]), .d(controlled_buffer_2_out[3]),
    .c(controlled_buffer_2_out[2]), .dp(controlled_buffer_2_out[7]));
  Register #(.trigger("falling")) register_6 (
    .D(Data), .en(register_2_q[2]), .clk(or_1_out), .Q(register_6_q));  // open: clr
  assign controlled_buffer_3_out = register_4_q[2] ? register_3_q : 8'bz;  // Controlled_Buffer controlled_buffer_3
  _7_Segment_Display u_7_segment_display_5 (
    .g(register_6_q[6]), .f(register_6_q[5]), .a(register_6_q[0]), .b(register_6_q[1]), .e(register_6_q[4]),
    .d(register_6_q[3]), .c(register_6_q[2]), .dp(register_6_q[7]));
  _7_Segment_Display u_7_segment_display_6 (
    .g(controlled_buffer_3_out[6]), .f(controlled_buffer_3_out[5]), .a(controlled_buffer_3_out[0]),
    .b(controlled_buffer_3_out[1]), .e(controlled_buffer_3_out[4]), .d(controlled_buffer_3_out[3]),
    .c(controlled_buffer_3_out[2]), .dp(controlled_buffer_3_out[7]));

  // Notes on the sheet:
  //   ADDRS - Adres segmentu
  //   ADDRD - Adres wyświetlacza
  //   Zero to stan aktywny
  //   To samo, tylko bufory 3 stanowee zamiast rejestrow
  //   Trzy multipleksowane wyświetlacze siedmiosegmentowe
endmodule
