// Logisim project 16042018.circ as structural Verilog: 1 circuit, main circuit main
module main (
  input  in_1,
  input  in_2,
  input  in_3,
  input  in_4,
  input  in_5,
  input  in_6,
  input  C,
  input  B,
  input  A,
  input  C_2,
  input  B_2,
  input  A_2,
  input  C_3,
  input  B_3,
  input  A_3,
  input  in_16,
  input  C_4,
  input  B_4,
  input  A_4,
  input  C_5,
  input  B_5,
  input  A_5,
  input  in_23,
  input  in_24,
  input  [1:0] in_25,
  input  [1:0] in_26,
  input  in_27,
  input  in_28,
  input  in_29,
  input  in_30,
  input  in_31,
  input  in_32,
  input  in_33,
  input  in_34,
  input  in_35,
  input  in_36,
  input  in_37,
  input  in_38,
  input  a0,
  input  a1,
  input  a2,
  input  b0,
  input  b1,
  input  b2,
  input  [2:0] in_45,
  input  G1,
  input  G2B,
  input  G2A,
  input  in_49,
  input  in_50,
  input  in_51,
  input  [2:0] in_52,
  output out_53,
  output out_54,
  output out_55,
  output out_56,
  output out_57,
  output out_58,
  output out_59,
  output out_60,
  output out_61,
  output out_62,
  output out_63,
  output out_64,
  output out_65,
  output out_66,
  output out_67,
  output out_68,
  output out_69,
  output out_70,
  output out_71,
  output out_72,
  output out_73,
  output out_74,
  output out_75,
  output out_76,
  output out_77,
  output out_78,
  output out_79,
  output out_80,
  output out_81,
  output out_82,
  output out_83,
  output out_84,
  output out_85,
  output out_86,
  output out_87,
  output out_88,
  output out_89,
  output out_90,
  output out_91,
  output out_92,
  output out_93,
  output out_94,
  output out_95,
  output out_96,
  output out_97,
  output out_98,
  output out_99,
  output out_100,
  output out_101,
  output out_102,
  output out_103,
  output out_104,
  output out_105,
  output out_106,
  output out_107,
  output out_108,
  output out_109,
  output out_110,
  output out_111,
  output out_112,
  output out_113,
  output out_114,
  output out_115,
  output out_116,
  output out_117,
  output out_118,
  output out_119,
  output out_120,
  output out_121,
  output out_122,
  output out_123,
  output out_124,
  output out_125,
  output out_126,
  output out_127,
  output out_128,
  output out_129,
  output out_130,
  output out_131,
  output out_132,
  output out_133,
  output out_134,
  output out_135,
  output out_136,
  output out_137,
  output out_138,
  output out_139,
  output out_140,
  output out_141,
  output out_142,
  output out_143,
  output out_144,
  output out_145,
  output out_146,
  output out_147,
  output out_148,
  output out_149,
  output out_150,
  output out_151,
  output out_152,
  output out_153,
  output out_154,
  output out_155,
  output out_156,
  output out_157,
  output out_158,
  output out_159,
  output out_160,
  output out_161,
  output out_162,
  output out_163,
  output out_164,
  output out_165,
  output out_166,
  output out_167,
  output out_168,
  output out_169
);

  wire and_17_out, and_18_out, and_19_out, and_20_out, and_21_out, and_22_out, and_23_out, and_24_out,
       and_25_out, and_26_out, clock_1_out, clock_2_out, clock_3_out, clock_4_out, clock_5_out, clock_6_out,
       clock_7_out, clock_8_out, clock_9_out, clock_10_out, clock_11_out, clock_12_out, clock_13_out,
       clock_14_out, clock_15_out, clock_16_out, clock_17_out, clock_18_out, clock_19_out, clock_20_out,
       clock_21_out, clock_22_out, clock_23_out, clock_24_out, clock_25_out, clock_26_out, clock_27_out,
       clock_28_out, clock_30_out, clock_31_out, clock_32_out, clock_33_out, controlled_buffer_1_out,
       decoder_2_out0, decoder_2_out1, decoder_2_out2, decoder_2_out3, decoder_2_out4, decoder_2_out5,
       decoder_2_out6, decoder_2_out7, decoder_3_out0, decoder_3_out1, decoder_3_out2, decoder_3_out3,
       decoder_3_out4, decoder_3_out5, decoder_3_out6, decoder_3_out7, decoder_4_out0, decoder_4_out1,
       decoder_4_out2, decoder_4_out3, decoder_4_out4, decoder_4_out5, decoder_4_out6, decoder_4_out7,
       not_1_out, not_2_out, not_3_out, not_4_out, not_5_out, not_6_out, not_7_out, not_8_out, not_9_out,
       not_10_out, not_11_out, not_12_out, not_13_out, not_14_out, not_15_out, not_16_out, not_17_out,
       not_18_out, not_19_out, not_20_out, not_21_out, not_23_out, or_3_out, or_12_out, or_13_out, or_14_out,
       or_15_out, xor_1_out, xor_2_out, xor_3_out, xor_4_out, xor_5_out;

  not not_1 (not_1_out, in_2);
  not not_2 (not_2_out, in_4);
  Clock clock_1 (.out(clock_1_out));
  not not_3 (not_3_out, in_3);
  not not_4 (not_4_out, in_5);
  not not_5 (not_5_out, C);
  not not_6 (not_6_out, C_2);
  not not_7 (not_7_out, in_1);
  and E (out_56, in_3, in_2);
  and Z (out_58, not_3_out, in_2);
  and I (out_60, not_1_out, in_3);
  and O (out_62, not_1_out, not_3_out);
  and and_1 (out_64, in_5, in_4);
  and and_2 (out_66, not_4_out, in_4);
  and and_3 (out_69, not_2_out, in_5);
  and and_4 (out_71, not_2_out, not_4_out);
  not not_8 (not_8_out, B);
  not not_9 (not_9_out, B_2);
  not not_10 (not_10_out, C_4);
  Decoder #(.select(2)) decoder_1 (
    .out0(out_132), .out1(out_133), .out2(out_134), .out3(out_135), .sel({in_29, in_28}), .en(in_23));
  and and_5 (out_53, clock_1_out, in_1);
  and and_6 (out_54, clock_1_out, not_7_out);
  not not_11 (not_11_out, in_6);
  not not_12 (not_12_out, A);
  not not_13 (not_13_out, A_2);
  not not_14 (not_14_out, C_3);
  not not_15 (not_15_out, B_4);
  Clock clock_2 (.out(clock_2_out));
  Clock clock_3 (.out(clock_3_out));
  Clock clock_4 (.out(clock_4_out));
  Clock clock_5 (.out(clock_5_out));
  Clock clock_6 (.out(clock_6_out));
  Clock clock_7 (.out(clock_7_out));
  and and_7 (out_72, clock_7_out, in_6);
  Clock clock_8 (.out(clock_8_out));
  and and_8 (out_74, clock_8_out, not_11_out);
  Clock clock_9 (.out(clock_9_out));
  not not_16 (not_16_out, B_3);
  not not_17 (not_17_out, A_4);
  not not_18 (not_18_out, C_5);
  and and_9 (out_55, clock_2_out, out_56);
  and and_10 (out_57, clock_2_out, out_58);
  and and_11 (out_59, clock_2_out, out_60);
  and and_12 (out_61, clock_2_out, out_62);
  and and_13 (out_63, clock_3_out, out_64);
  and and_14 (out_65, clock_4_out, out_66);
  and and_15 (out_68, clock_5_out, out_69);
  and and_16 (out_70, clock_6_out, out_71);
  or or_1 (out_73, out_72, out_74);
  nand o7 (out_76, C, B, A);
  nand o6 (out_78, C, B, not_12_out);
  nand o5 (out_80, C, not_8_out, A);
  nand o4 (out_82, C, not_8_out, not_12_out);
  nand o3 (out_84, not_5_out, B, A);
  nand o2 (out_86, not_5_out, B, not_12_out);
  nand o1 (out_88, not_5_out, not_8_out, A);
  nand o0 (out_90, not_5_out, not_8_out, not_12_out);
  nand o7_2 (out_92, C_2, B_2, A_2);
  nand o6_2 (out_94, C_2, B_2, not_13_out);
  nand o5_2 (out_96, C_2, not_9_out, A_2);
  nand o4_2 (out_98, C_2, not_9_out, not_13_out);
  nand o3_2 (out_101, not_6_out, B_2, A_2);
  nand o2_2 (out_103, not_6_out, B_2, not_13_out);
  nand o1_2 (out_105, not_6_out, not_9_out, A_2);
  nand o0_2 (out_107, not_6_out, not_9_out, not_13_out);
  not not_19 (not_19_out, A_3);
  not not_20 (not_20_out, B_5);
  xor S (out_143, in_32, in_31);
  and sC (out_145, in_31, in_32);
  Clock clock_10 (.out(clock_10_out));
  buf and_17 (and_17_out, ~in_51);  // AND_Gate AND_Gate
  or or_2 (out_67, out_63, out_65, out_68, out_70);
  nand o7_3 (out_108, C_3, B_3, A_3);
  nand o6_3 (out_109, C_3, B_3, not_19_out);
  nand o5_3 (out_110, C_3, not_16_out, A_3);
  nand o4_3 (out_111, C_3, not_16_out, not_19_out);
  nand o3_3 (out_112, not_14_out, B_3, A_3);
  nand o2_3 (out_113, not_14_out, B_3, not_19_out);
  nand o1_3 (out_114, not_14_out, not_16_out, A_3);
  nand o0_3 (out_115, not_14_out, not_16_out, not_19_out);
  nand o7_4 (out_116, C_4, B_4, A_4);
  nand o6_4 (out_117, C_4, B_4, not_17_out);
  nand o5_4 (out_118, C_4, not_15_out, A_4);
  nand o4_4 (out_119, C_4, not_15_out, not_17_out);
  nand o3_4 (out_120, not_10_out, B_4, A_4);
  nand o2_4 (out_121, not_10_out, B_4, not_17_out);
  nand o1_4 (out_122, not_10_out, not_15_out, A_4);
  nand o0_4 (out_123, not_10_out, not_15_out, not_17_out);
  Clock clock_11 (.out(clock_11_out));
  not not_21 (not_21_out, A_5);
  Decoder #(.select(3)) decoder_2 (
    .out0(decoder_2_out0), .out1(decoder_2_out1), .out2(decoder_2_out2), .out3(decoder_2_out3),
    .out4(decoder_2_out4), .out5(decoder_2_out5), .out6(decoder_2_out6), .out7(decoder_2_out7), .sel(in_52),
    .en(and_17_out));
  not not_22 (out_154, decoder_2_out7);
  Clock clock_12 (.out(clock_12_out));
  Clock #(.highDuration(3)) clock_13 (.out(clock_13_out));
  Clock #(.highDuration(3), .lowDuration(3)) clock_14 (.out(clock_14_out));
  Clock #(.highDuration(2), .lowDuration(3)) clock_15 (.out(clock_15_out));
  Clock #(.lowDuration(3)) clock_16 (.out(clock_16_out));
  Clock #(.highDuration(2), .lowDuration(2)) clock_17 (.out(clock_17_out));
  Clock #(.highDuration(2)) clock_18 (.out(clock_18_out));
  Clock #(.lowDuration(2)) clock_19 (.out(clock_19_out));
  nand o7_5 (out_124, C_5, B_5, A_5, clock_11_out);
  nand o6_5 (out_125, C_5, B_5, not_21_out, clock_11_out);
  nand o5_5 (out_126, C_5, not_20_out, A_5, clock_11_out);
  nand o4_5 (out_127, C_5, not_20_out, not_21_out, clock_11_out);
  nand o3_5 (out_128, not_18_out, B_5, A_5, clock_11_out);
  nand o2_5 (out_129, not_18_out, B_5, not_21_out, clock_11_out);
  nand o1_5 (out_130, not_18_out, not_20_out, A_5, clock_11_out);
  nand o0_5 (out_131, not_18_out, not_20_out, not_21_out, clock_11_out);
  Clock clock_20 (.out(clock_20_out));
  assign controlled_buffer_1_out = in_36 ? in_34 : 1'bz;  // Controlled_Buffer controlled_buffer_1
  assign controlled_buffer_1_out = in_38 ? in_37 : 1'bz;  // Controlled_Buffer controlled_buffer_2
  and and_18 (and_18_out, ~clock_10_out, ~G2B, ~G2A);  // AND_Gate
  not not_23 (not_23_out, in_49);
  not not_24 (out_156, decoder_2_out5);
  not not_25 (out_155, decoder_2_out6);
  nor nor_1 (out_75, out_76, clock_9_out);
  nor nor_2 (out_77, out_78, clock_9_out);
  nor nor_3 (out_79, out_80, clock_9_out);
  nor nor_4 (out_81, out_82, clock_9_out);
  nor nor_5 (out_83, out_84, clock_9_out);
  nor nor_6 (out_85, out_86, clock_9_out);
  nor nor_7 (out_87, out_88, clock_9_out);
  nor nor_8 (out_89, out_90, clock_9_out);
  nor nor_9 (out_91, out_92, clock_12_out);
  nor nor_10 (out_93, out_94, clock_13_out);
  nor nor_11 (out_95, out_96, clock_14_out);
  nor nor_12 (out_97, out_98, clock_15_out);
  nor nor_13 (out_100, out_101, clock_16_out);
  nor nor_14 (out_102, out_103, clock_17_out);
  nor nor_15 (out_104, out_105, clock_18_out);
  nor nor_16 (out_106, out_107, clock_19_out);
  Clock clock_21 (.out(clock_21_out));
  Clock #(.highDuration(3)) clock_22 (.out(clock_22_out));
  Clock #(.highDuration(3), .lowDuration(3)) clock_23 (.out(clock_23_out));
  Clock #(.highDuration(2), .lowDuration(3)) clock_24 (.out(clock_24_out));
  Clock #(.lowDuration(3)) clock_25 (.out(clock_25_out));
  Clock #(.highDuration(2), .lowDuration(2)) clock_26 (.out(clock_26_out));
  Clock #(.highDuration(2)) clock_27 (.out(clock_27_out));
  Clock #(.lowDuration(2)) clock_28 (.out(clock_28_out));
  Clock clock_29 ();  // open: out
  Demultiplexer #(.select(2)) demultiplexer_1 (
    .out0(out_136), .out1(out_137), .out2(out_138), .out3(out_140), .in(clock_20_out), .sel(in_26), .en(in_24));
  xor S_2 (out_141, out_143, in_30);
  and sC_2 (out_142, in_30, out_143);
  assign controlled_buffer_1_out = in_33 ? in_35 : 1'bz;  // Controlled_Buffer controlled_buffer_3
  Decoder #(.select(3)) decoder_3 (
    .out0(decoder_3_out0), .out1(decoder_3_out1), .out2(decoder_3_out2), .out3(decoder_3_out3),
    .out4(decoder_3_out4), .out5(decoder_3_out5), .out6(decoder_3_out6), .out7(decoder_3_out7), .sel(in_45),
    .en(and_18_out));
  not not_26 (out_146, decoder_3_out7);
  and and_19 (and_19_out, ~not_23_out, ~in_51, ~in_50);  // AND_Gate
  not not_27 (out_157, decoder_2_out4);
  not not_28 (out_159, decoder_2_out2);
  not not_29 (out_158, decoder_2_out3);
  or or_3 (or_3_out, out_108, clock_21_out);
  or or_4 (or_3_out, out_109, clock_22_out);
  or or_5 (or_3_out, out_110, clock_23_out);
  or or_6 (or_3_out, out_111, clock_24_out);
  or or_7 (or_3_out, out_112, clock_25_out);
  or or_8 (or_3_out, out_113, clock_26_out);
  or or_9 (or_3_out, out_114, clock_27_out);
  or or_10 (or_3_out, out_115, clock_28_out);
  or or_11 (out_144, out_142, out_145);
  xor xor_1 (xor_1_out, b0, a0);
  and and_20 (and_20_out, b0, a0);
  not not_30 (out_147, decoder_3_out6);
  not not_31 (out_148, decoder_3_out5);
  Decoder #(.select(3)) decoder_4 (
    .out0(decoder_4_out0), .out1(decoder_4_out1), .out2(decoder_4_out2), .out3(decoder_4_out3),
    .out4(decoder_4_out4), .out5(decoder_4_out5), .out6(decoder_4_out6), .out7(decoder_4_out7), .sel(in_52),
    .en(and_19_out));
  not not_32 (out_161, decoder_2_out0);
  not not_33 (out_160, decoder_2_out1);
  not not_34 (out_162, decoder_4_out7);
  or or_12 (or_12_out, out_91, out_93, out_95, out_97);
  or or_13 (or_13_out, out_100, out_102, out_104, out_106);
  Pull_Resistor #(.pull(1)) pull_resistor_1 (.node(or_3_out));
  not not_35 (out_150, decoder_3_out3);
  not not_36 (out_151, decoder_3_out2);
  not not_37 (out_149, decoder_3_out4);
  not not_38 (out_164, decoder_4_out5);
  not not_39 (out_163, decoder_4_out6);
  nor nor_17 (out_99, or_12_out, or_13_out);
  xor xor_2 (xor_2_out, b1, a1);
  and and_21 (and_21_out, a1, b1);
  and and_22 (and_22_out, a1, and_20_out);
  and and_23 (and_23_out, b1, and_20_out);
  xor xor_3 (xor_3_out, b2, a2);
  and and_24 (and_24_out, a2, b2);
  and and_25 (and_25_out, a2, or_14_out);
  and and_26 (and_26_out, b2, or_14_out);
  not not_40 (out_152, decoder_3_out1);
  not not_41 (out_153, decoder_3_out0);
  not not_42 (out_166, decoder_4_out3);
  not not_43 (out_165, decoder_4_out4);
  not not_44 (out_167, decoder_4_out2);
  Clock #(.lowDuration(3)) clock_30 (.out(clock_30_out));
  Clock #(.highDuration(3)) clock_31 (.out(clock_31_out));
  Clock #(.highDuration(2)) clock_32 (.out(clock_32_out));
  xor xor_4 (xor_4_out, and_20_out, xor_2_out);
  or or_14 (or_14_out, and_21_out, and_22_out, and_23_out);
  xor xor_5 (xor_5_out, or_14_out, xor_3_out);
  or or_15 (or_15_out, and_24_out, and_25_out, and_26_out);
  not not_45 (out_168, decoder_4_out1);
  not not_46 (out_169, decoder_4_out0);
  Clock #(.lowDuration(2)) clock_33 (.out(clock_33_out));
  Multiplexer #(.select(2)) multiplexer_1 (
    .in0(clock_30_out), .in1(clock_31_out), .in2(clock_32_out), .in3(clock_33_out), .out(out_139),
    .sel(in_25), .en(in_27));

  // Notes on the sheet:
  //   demulitiplekser
  //   dekoder
  //   do tego miejsca
  //   dekoder
  //   do tego miejsca
  //   multiplekser
  //   To chyba ma byc aktywowane zerem
  //   demul 2bitowy lub "1 z 4"
  //   multiplekser 2bitowy lub "1 z 4"
  //   Demultiplekser 3 bitowy
  //   Multiplekser 3 bitowy
  //   Dekoder 3b
  //   Ulepszony multiplekser 3b
  //   Stan wysokiej impedancji (floating)
  //   Tu sie zaczynaja sumatory
  //   2x138
  //   Można stworzyć magistralę danych. Tylko jeden "dodatkowy" bit musi być "zaświecony", reszta floating
  //   Sumator 3 bitowy
  //   Cos na ksztalt 138
  //   or_3 drives only 0 and floats otherwise
  //   or_4 drives only 0 and floats otherwise
  //   or_5 drives only 0 and floats otherwise
  //   or_6 drives only 0 and floats otherwise
  //   or_7 drives only 0 and floats otherwise
  //   or_8 drives only 0 and floats otherwise
  //   or_9 drives only 0 and floats otherwise
  //   or_10 drives only 0 and floats otherwise
  //   Z tego co pamietam, to ten sprzecior nie dziala!
endmodule
