// Logisim project 16052018.circ as structural Verilog: 1 circuit, main circuit main
module main (
  input  c,
  input  b,
  input  a,
  input  in_4,
  input  in_5,
  input  c_2,
  input  b_2,
  input  a_2,
  input  [2:0] in_9,
  output out_10,
  output out_11,
  output out_12,
  output out_13,
  output out_14,
  output CARRY_a_b_c
);

  wire and_1_out, and_2_out, and_3_out, and_4_out, and_5_out, and_6_out, and_7_out, and_8_out, and_9_out,
       multiplexer_1_out, not_1_out, not_2_out, not_3_out, or_1_out, xor_1_out, xor_2_out, xor_3_out;

  xor xor_1 (xor_1_out, b, a);
  and and_1 (and_1_out, a, b);
  and and_2 (and_2_out, b, c);
  and and_3 (and_3_out, a, c);
  xor xor_2 (xor_2_out, in_4, in_5);
  and and_4 (and_4_out, in_5, in_4);
  and and_5 (and_5_out, in_4, out_11);
  and and_6 (and_6_out, in_5, out_11);
  not not_1 (not_1_out, or_1_out);
  or or_1 (or_1_out, a_2, b_2);
  not not_2 (not_2_out, a_2);
  xor xor_3 (xor_3_out, b_2, a_2);
  and and_7 (and_7_out, a_2, b_2);
  not not_3 (not_3_out, and_7_out);
  and and_8 (and_8_out, b_2, c_2);
  and and_9 (and_9_out, a_2, c_2);
  xor xor_4 (out_10, c, xor_1_out);
  or or_2 (out_11, and_1_out, and_2_out, and_3_out);
  xor xor_5 (out_12, out_11, xor_2_out);
  or or_3 (out_13, and_4_out, and_5_out, and_6_out);
  xor xor_6 (out_14, c_2, xor_3_out);
  or or_4 (CARRY_a_b_c, and_7_out, and_8_out, and_9_out);
  Multiplexer #(.select(3), .enable("false")) multiplexer_1 (
    .in0(not_1_out), .in1(or_1_out), .in2(not_2_out), .in3(out_14), .in4(xor_3_out), .in5(and_7_out),
    .in6(not_3_out), .in7(CARRY_a_b_c), .out(multiplexer_1_out), .sel(in_9));

  // Notes on the sheet:
  //   Sumator 3b
  //   Arithmetic Logic Unit
  //   NOR(a,b)
  //   OR(a,b)
  //   NOT(a)
  //   SUM(a,b,c)
  //   XOR(a,b,c)
  //   AND(a,b)
  //   NAND(a,b)
endmodule
