// Logisim project 18062018.circ as structural Verilog: 1 circuit, main circuit main
module main (
  input  A0,
  input  in_2,
  input  in_3,
  input  in_4,
  input  in_5,
  input  in_6,
  input  in_7,
  input  A7,
  input  WR,
  input  IORQ,
  input  RD,
  input  in_12,
  input  in_13,
  input  in_14,
  input  in_15,
  input  in_16,
  input  in_17,
  input  in_18,
  input  in_19,
  input  in_20,
  input  in_21,
  input  in_22,
  input  in_23,
  input  in_24,
  input  in_25,
  input  A0_2,
  input  in_27,
  input  in_28,
  input  in_29,
  input  in_30,
  input  in_31,
  input  in_32,
  input  A7_2,
  input  WR_2,
  input  IORQ_2,
  input  RD_2,
  input  in_37,
  input  in_38,
  input  in_39,
  input  in_40,
  input  in_41,
  input  in_42,
  input  in_43,
  input  in_44,
  input  in_45,
  input  in_46,
  input  in_47,
  input  in_48,
  input  in_49,
  input  in_50,
  input  in_51,
  output out_52,
  output out_53,
  output out_54
);

  wire buffer_1_out, buffer_2_out, buffer_3_out, nor_1_out, nor_2_out, or_1_out, or_2_out, or_3_out,
       or_4_out, or_5_out, or_6_out, transistor_1_out, transistor_2_out, transistor_3_out, transistor_4_out,
       transistor_5_out, transistor_6_out;
  wire [7:0] register_1_q;

  or or_1 (or_1_out, in_4, ~in_5, in_6, ~in_7, A7);  // OR_Gate
  or or_2 (or_2_out, WR, IORQ);
  or or_3 (or_3_out, IORQ, RD);
  or or_4 (or_4_out, in_29, ~in_30, in_31, ~in_32, A7_2);  // OR_Gate
  or or_5 (or_5_out, WR_2, IORQ_2);
  or or_6 (or_6_out, IORQ_2, RD_2);
  Register #(.trigger("falling")) register_1 (
    .D({{5{1'b0}}, in_39, in_38, in_37}), .en(in_41), .clk(or_5_out), .Q(register_1_q));  // open: clr
  nor nor_1 (nor_1_out, or_3_out, or_1_out);
  assign out_52 = nor_1_out ? transistor_1_out : 1'bz;  // Controlled_Buffer controlled_buffer_1
  assign out_53 = nor_1_out ? transistor_2_out : 1'bz;  // Controlled_Buffer controlled_buffer_2
  assign out_54 = nor_1_out ? transistor_3_out : 1'bz;  // Controlled_Buffer controlled_buffer_3
  nor nor_2 (nor_2_out, or_6_out, or_4_out);
  Transistor #(.\type ("n")) transistor_1 (.in(in_3), .out(transistor_1_out), .gate(in_12));
  Transistor #(.\type ("n")) transistor_2 (.in(in_3), .out(transistor_2_out), .gate(in_15));
  Transistor #(.\type ("n")) transistor_3 (.in(in_3), .out(transistor_3_out), .gate(in_22));
  buf buffer_1 (buffer_1_out, register_1_q[2]);
  Transistor #(.\type ("n")) transistor_4 (.in(buffer_1_out), .out(transistor_4_out), .gate(in_43));
  Transistor #(.\type ("n")) transistor_5 (.in(buffer_1_out), .out(transistor_5_out), .gate(in_46));
  Transistor #(.\type ("n")) transistor_6 (.in(buffer_1_out), .out(transistor_6_out), .gate(in_49));
  Transistor #(.\type ("n")) transistor_7 (.in(in_2), .out(transistor_1_out), .gate(in_13));
  Transistor #(.\type ("n")) transistor_8 (.in(in_2), .out(transistor_2_out), .gate(in_16));
  Transistor #(.\type ("n")) transistor_9 (.in(in_2), .out(transistor_3_out), .gate(in_23));
  buf buffer_2 (buffer_2_out, register_1_q[1]);
  Transistor #(.\type ("n")) transistor_10 (.in(buffer_2_out), .out(transistor_4_out), .gate(in_44));
  Transistor #(.\type ("n")) transistor_11 (.in(buffer_2_out), .out(transistor_5_out), .gate(in_47));
  Transistor #(.\type ("n")) transistor_12 (.in(buffer_2_out), .out(transistor_6_out), .gate(in_50));
  Pull_Resistor #(.pull(1)) pull_resistor_1 (.node(transistor_1_out));
  Transistor #(.\type ("n")) transistor_13 (.in(A0), .out(transistor_1_out), .gate(in_14));
  Transistor #(.\type ("n")) transistor_14 (.in(A0), .out(transistor_2_out), .gate(in_17));
  Transistor #(.\type ("n")) transistor_15 (.in(A0), .out(transistor_3_out), .gate(in_24));
  buf buffer_3 (buffer_3_out, register_1_q[0]);
  Pull_Resistor #(.pull(1)) pull_resistor_2 (.node(transistor_4_out));
  Transistor #(.\type ("n")) transistor_16 (.in(buffer_3_out), .out(transistor_4_out), .gate(in_45));
  Transistor #(.\type ("n")) transistor_17 (.in(buffer_3_out), .out(transistor_5_out), .gate(in_48));
  Transistor #(.\type ("n")) transistor_18 (.in(buffer_3_out), .out(transistor_6_out), .gate(in_51));
  Pull_Resistor #(.pull(1)) pull_resistor_3 (.node(transistor_3_out));
  Pull_Resistor #(.pull(1)) pull_resistor_4 (.node(transistor_2_out));
  Pull_Resistor #(.pull(1)) pull_resistor_5 (.node(transistor_5_out));
  Pull_Resistor #(.pull(1)) pull_resistor_6 (.node(transistor_6_out));
  // AND_Gate and_1 is placed but not wired

  // Notes on the sheet:
  //   Klawiatura rozpoznaje ten adres
  //   Klawiatura rozpoznaje ten adres
  //   Klawiatura, linia aktywowana zerem
  //   Dokończone w 20062018.circ
  //   buffer_1 drives only 1 and floats otherwise
  //   buffer_2 drives only 1 and floats otherwise
  //   buffer_3 drives only 1 and floats otherwise
endmodule
