// Logisim project 20062018.circ as structural Verilog: 1 circuit, main circuit main
module main (
  input  A0,
  input  A1,
  input  A2,
  input  A3,
  input  ADDR,
  input  IORQ,
  input  RD,
  input  in_8,
  input  in_9,
  input  in_10,
  input  in_11,
  input  in_12,
  input  in_13,
  input  in_14,
  input  in_15,
  input  in_16,
  input  in_17,
  input  in_18,
  input  in_19,
  input  in_20,
  input  in_21,
  input  in_22,
  input  in_23,
  input  [7:0] D7D0OUT,
  input  in_25,
  input  WR,
  input  ADDR_2,
  input  IORQ_2,
  input  in_29,
  input  in_30,
  input  in_31,
  input  in_32,
  input  RD_2,
  input  in_34,
  input  in_35,
  input  in_36,
  input  in_37,
  input  in_38,
  input  in_39,
  input  in_40,
  input  in_41,
  input  in_42,
  input  in_43,
  input  in_44,
  input  in_45,
  output [3:0] D3D0,
  output [3:0] D3D0_2
);

  wire buffer_1_out, buffer_2_out, buffer_3_out, buffer_4_out, buffer_5_out, buffer_6_out, buffer_7_out,
       buffer_8_out, nor_1_out, nor_2_out, or_1_out, transistor_1_out, transistor_2_out, transistor_3_out,
       transistor_4_out, transistor_17_out, transistor_18_out, transistor_19_out, transistor_20_out;
  wire [7:0] register_1_q;

  nor nor_1 (nor_1_out, ADDR, IORQ, RD);
  assign D3D0[0] = nor_1_out ? transistor_1_out : 1'bz;  // Controlled_Buffer controlled_buffer_1
  assign D3D0[1] = nor_1_out ? transistor_2_out : 1'bz;  // Controlled_Buffer controlled_buffer_2
  assign D3D0[2] = nor_1_out ? transistor_3_out : 1'bz;  // Controlled_Buffer controlled_buffer_3
  assign D3D0[3] = nor_1_out ? transistor_4_out : 1'bz;  // Controlled_Buffer controlled_buffer_4
  buf buffer_1 (buffer_1_out, A3);
  Transistor #(.\type ("n")) transistor_1 (.in(buffer_1_out), .out(transistor_1_out), .gate(in_8));
  Transistor #(.\type ("n")) transistor_2 (.in(buffer_1_out), .out(transistor_2_out), .gate(in_12));
  Transistor #(.\type ("n")) transistor_3 (.in(buffer_1_out), .out(transistor_3_out), .gate(in_16));
  Transistor #(.\type ("n")) transistor_4 (.in(buffer_1_out), .out(transistor_4_out), .gate(in_20));
  or or_1 (or_1_out, IORQ_2, ADDR_2, WR);
  nor nor_2 (nor_2_out, ADDR_2, IORQ_2, RD_2);
  buf buffer_2 (buffer_2_out, A2);
  Transistor #(.\type ("n")) transistor_5 (.in(buffer_2_out), .out(transistor_1_out), .gate(in_9));
  Transistor #(.\type ("n")) transistor_6 (.in(buffer_2_out), .out(transistor_2_out), .gate(in_13));
  Transistor #(.\type ("n")) transistor_7 (.in(buffer_2_out), .out(transistor_3_out), .gate(in_17));
  Transistor #(.\type ("n")) transistor_8 (.in(buffer_2_out), .out(transistor_4_out), .gate(in_21));
  Register #(.trigger("falling")) register_1 (.D(D7D0OUT), .en(in_25), .clk(or_1_out), .Q(register_1_q));  // open: clr
  buf buffer_3 (buffer_3_out, A1);
  Transistor #(.\type ("n")) transistor_9 (.in(buffer_3_out), .out(transistor_1_out), .gate(in_10));
  Transistor #(.\type ("n")) transistor_10 (.in(buffer_3_out), .out(transistor_2_out), .gate(in_14));
  Transistor #(.\type ("n")) transistor_11 (.in(buffer_3_out), .out(transistor_3_out), .gate(in_18));
  Transistor #(.\type ("n")) transistor_12 (.in(buffer_3_out), .out(transistor_4_out), .gate(in_22));
  assign D3D0_2[0] = nor_2_out ? transistor_17_out : 1'bz;  // Controlled_Buffer controlled_buffer_5
  assign D3D0_2[1] = nor_2_out ? transistor_18_out : 1'bz;  // Controlled_Buffer controlled_buffer_6
  assign D3D0_2[2] = nor_2_out ? transistor_19_out : 1'bz;  // Controlled_Buffer controlled_buffer_7
  assign D3D0_2[3] = nor_2_out ? transistor_20_out : 1'bz;  // Controlled_Buffer controlled_buffer_8
  Pull_Resistor #(.pull(1)) pull_resistor_1 (.node(transistor_1_out));
  buf buffer_4 (buffer_4_out, A0);
  Transistor #(.\type ("n")) transistor_13 (.in(buffer_4_out), .out(transistor_1_out), .gate(in_11));
  Transistor #(.\type ("n")) transistor_14 (.in(buffer_4_out), .out(transistor_2_out), .gate(in_15));
  Transistor #(.\type ("n")) transistor_15 (.in(buffer_4_out), .out(transistor_3_out), .gate(in_19));
  Transistor #(.\type ("n")) transistor_16 (.in(buffer_4_out), .out(transistor_4_out), .gate(in_23));
  buf buffer_5 (buffer_5_out, register_1_q[3]);
  Transistor #(.\type ("n")) transistor_17 (.in(buffer_5_out), .out(transistor_17_out), .gate(in_29));
  Transistor #(.\type ("n")) transistor_18 (.in(buffer_5_out), .out(transistor_18_out), .gate(in_34));
  Transistor #(.\type ("n")) transistor_19 (.in(buffer_5_out), .out(transistor_19_out), .gate(in_38));
  Transistor #(.\type ("n")) transistor_20 (.in(buffer_5_out), .out(transistor_20_out), .gate(in_42));
  Pull_Resistor #(.pull(1)) pull_resistor_2 (.node(transistor_2_out));
  Pull_Resistor #(.pull(1)) pull_resistor_3 (.node(transistor_3_out));
  buf buffer_6 (buffer_6_out, register_1_q[2]);
  Transistor #(.\type ("n")) transistor_21 (.in(buffer_8_out), .out(transistor_17_out), .gate(in_31));
  Transistor #(.\type ("n")) transistor_22 (.in(buffer_6_out), .out(transistor_17_out), .gate(in_30));
  Transistor #(.\type ("n")) transistor_23 (.in(buffer_8_out), .out(transistor_18_out), .gate(in_36));
  Transistor #(.\type ("n")) transistor_24 (.in(buffer_6_out), .out(transistor_18_out), .gate(in_35));
  Transistor #(.\type ("n")) transistor_25 (.in(buffer_8_out), .out(transistor_19_out), .gate(in_40));
  Transistor #(.\type ("n")) transistor_26 (.in(buffer_6_out), .out(transistor_19_out), .gate(in_39));
  Transistor #(.\type ("n")) transistor_27 (.in(buffer_8_out), .out(transistor_20_out), .gate(in_44));
  Transistor #(.\type ("n")) transistor_28 (.in(buffer_6_out), .out(transistor_20_out), .gate(in_43));
  Pull_Resistor #(.pull(1)) pull_resistor_4 (.node(transistor_4_out));
  buf buffer_7 (buffer_7_out, register_1_q[0]);
  buf buffer_8 (buffer_8_out, register_1_q[1]);
  Transistor #(.\type ("n")) transistor_29 (.in(buffer_7_out), .out(transistor_17_out), .gate(in_32));
  Transistor #(.\type ("n")) transistor_30 (.in(buffer_7_out), .out(transistor_18_out), .gate(in_37));
  Transistor #(.\type ("n")) transistor_31 (.in(buffer_7_out), .out(transistor_19_out), .gate(in_41));
  Transistor #(.\type ("n")) transistor_32 (.in(buffer_7_out), .out(transistor_20_out), .gate(in_45));
  Pull_Resistor pull_resistor_5 (.node(transistor_17_out));
  Pull_Resistor pull_resistor_6 (.node(transistor_18_out));
  Pull_Resistor pull_resistor_7 (.node(transistor_20_out));
  Pull_Resistor pull_resistor_8 (.node(transistor_19_out));
  // NOT_Gate not_1 is placed but not wired

  // Notes on the sheet:
  //   Klawiatura, model pierwszy, marnuje 12 adresow
  //   buffer_1 drives only 0 and floats otherwise
  //   buffer_2 drives only 0 and floats otherwise
  //   buffer_3 drives only 0 and floats otherwise
  //   buffer_4 drives only 0 and floats otherwise
  //   buffer_5 drives only 1 and floats otherwise
  //   buffer_6 drives only 1 and floats otherwise
  //   buffer_7 drives only 1 and floats otherwise
  //   buffer_8 drives only 1 and floats otherwise
endmodule
