// Logisim project 21052018.circ as structural Verilog: 1 circuit, main circuit main
module main (
  input  R,
  input  S,
  input  S_2,
  input  R_2,
  input  S_3,
  input  R_3,
  input  S_4,
  input  CLK,
  input  R_4,
  input  S_5,
  input  CLK_2,
  input  R_5,
  input  D,
  input  CLK_3,
  input  D_2,
  input  CLK_4,
  input  S_6,
  input  CLK_5,
  input  R_6,
  input  in_20,
  input  CLK_6,
  input  S_7,
  input  CLK_7,
  input  S_8,
  input  R_7,
  input  in_26,
  input  in_27,
  input  CLK_8,
  input  in_29,
  input  in_30,
  input  in_31,
  input  in_32,
  input  in_33,
  input  in_34,
  input  in_35,
  input  in_36,
  input  in_37,
  input  in_38,
  input  in_39,
  input  in_40,
  input  in_41,
  input  in_42,
  input  in_43,
  input  in_44,
  input  in_45,
  input  in_46,
  input  in_47,
  input  in_48,
  input  in_49,
  input  in_50,
  input  in_51,
  input  in_52,
  input  \T_pełny ,
  input  in_54,
  input  in_55,
  output Q,
  output Q_2,
  output Q_3,
  output Q_4,
  output Q_5,
  output Q_6,
  output Q_7,
  output Q_8,
  output Q_9,
  output Q_10,
  output Q_11,
  output Q_12,
  output Q_13,
  output Q_14,
  output Q_15,
  output Q_16,
  output Q_17,
  output Q_18,
  output Q_19,
  output Q_20,
  output Q_21,
  output Q_22,
  output Q_23,
  output Q_24,
  output Q_25,
  output Q_26,
  output Q_27,
  output Q_28,
  output Q_29,
  output Q_30,
  output out_86,
  output out_87,
  output Q_31,
  output Q_32,
  output out_90,
  output out_91,
  output out_92,
  output out_93
);

  wire and_1_out, and_2_out, and_3_out, and_4_out, and_5_out, and_6_out, clock_1_out, d_ff_1_q, d_ff_2_qn,
       d_ff_3_qn, d_ff_4_q, d_ff_5_q, d_ff_6_q, d_ff_7_q, d_ff_8_qn, d_ff_9_q, j_k_ff_2_q, j_k_ff_2_qn,
       nand_3_out, nand_4_out, nand_5_out, nand_6_out, nand_7_out, nand_8_out, nand_9_out, nand_10_out,
       nand_11_out, nand_12_out, nand_13_out, nand_14_out, nand_19_out, nand_20_out, nand_27_out,
       nand_28_out, nand_31_out, nand_32_out, nand_39_out, nand_40_out, nand_41_out, nand_42_out,
       nand_43_out, nand_44_out, nand_49_out, nand_50_out, nand_53_out, nand_54_out, not_1_out, not_2_out,
       not_3_out, not_4_out, not_5_out, not_6_out, not_7_out, not_8_out, not_9_out, not_10_out, s_r_ff_1_q,
       s_r_ff_1_qn, s_r_ff_2_q, s_r_ff_2_qn, s_r_ff_3_q, s_r_ff_3_qn, s_r_ff_4_q, s_r_ff_5_q, s_r_ff_5_qn,
       t_ff_3_q, undriven, undriven_2, xnor_1_out, xor_1_out, xor_2_out, xor_3_out, xor_4_out;

  Clock clock_1 (.out(clock_1_out));
  nor nor_1 (Q, R, Q_2);
  nor nor_2 (Q_2, Q, S);
  nand nand_1 (Q_3, S_2, Q_4);
  nand nand_2 (Q_4, Q_3, R_2);
  nand nand_3 (nand_3_out, S_3, S_3);
  nand nand_4 (nand_4_out, R_3, R_3);
  nand nand_5 (nand_5_out, S_4, CLK);
  nand nand_6 (nand_6_out, CLK, R_4);
  nand nand_7 (nand_7_out, D, CLK_3);
  not not_1 (not_1_out, D);
  nand nand_8 (nand_8_out, CLK_3, not_1_out);
  nand nand_9 (nand_9_out, D_2, CLK_4);
  not not_2 (not_2_out, D_2);
  nand nand_10 (nand_10_out, CLK_4, not_2_out);
  nand nand_11 (nand_11_out, S_6, ~R_6, CLK_5);  // NAND_Gate
  nand nand_12 (nand_12_out, CLK_5, ~S_6, R_6);  // NAND_Gate
  and and_1 (and_1_out, CLK_6, clock_1_out);
  not not_3 (not_3_out, Q_24);
  nand nand_13 (nand_13_out, Q_28, ~Q_26, CLK_7);  // NAND_Gate
  nand nand_14 (nand_14_out, CLK_7, ~Q_28, Q_26);  // NAND_Gate
  and and_2 (and_2_out, Q_32, in_26);
  and and_3 (and_3_out, in_30, Q_30);
  xor xor_1 (xor_1_out, in_47, s_r_ff_1_qn);
  S_R_Flip_Flop s_r_ff_1 (
    .S(xor_1_out), .R(xor_2_out), .clk(in_49), .Q(s_r_ff_1_q), .Qn(s_r_ff_1_qn));  // open: reset, preset
  xor xor_2 (xor_2_out, s_r_ff_1_q, in_47);
  nand nand_15 (Q_5, nand_3_out, Q_6);
  nand nand_16 (Q_6, Q_5, nand_4_out);
  nand nand_17 (Q_7, nand_5_out, Q_8);
  nand nand_18 (Q_8, Q_7, nand_6_out);
  nand nand_19 (nand_19_out, S_5, ~R_5, CLK_2);  // NAND_Gate
  nand nand_20 (nand_20_out, CLK_2, ~S_5, R_5);  // NAND_Gate
  nand nand_21 (Q_11, nand_7_out, Q_12);
  nand nand_22 (Q_12, Q_11, nand_8_out);
  nand nand_23 (Q_13, nand_9_out, Q_15);
  nand nand_24 (Q_15, Q_13, nand_10_out);
  nand nand_25 (Q_17, nand_11_out, Q_19);
  nand nand_26 (Q_19, Q_17, nand_12_out);
  nand nand_27 (nand_27_out, Q_24, and_1_out);
  nand nand_28 (nand_28_out, and_1_out, not_3_out);
  nand nand_29 (Q_25, nand_13_out, Q_27);
  nand nand_30 (Q_27, Q_25, nand_14_out);
  nand nand_31 (nand_31_out, and_2_out, ~and_3_out, CLK_8);  // NAND_Gate
  nand nand_32 (nand_32_out, CLK_8, ~and_2_out, and_3_out);  // NAND_Gate
  D_Flip_Flop #(.trigger("falling")) d_ff_1 (.D(in_31), .clk(in_32), .Q(d_ff_1_q));  // open: Qn, preset, reset
  xor xor_3 (xor_3_out, in_33, d_ff_2_qn);
  D_Flip_Flop d_ff_2 (.D(xor_3_out), .clk(in_34), .Q(out_90), .Qn(d_ff_2_qn));  // open: preset, reset
  xor xor_4 (xor_4_out, in_35, s_r_ff_2_qn);
  S_R_Flip_Flop s_r_ff_2 (
    .S(xor_4_out), .R(s_r_ff_2_q), .clk(in_40), .Q(s_r_ff_2_q), .Qn(s_r_ff_2_qn));  // open: reset, preset
  xnor xnor_1 (xnor_1_out, in_51, d_ff_3_qn);
  D_Flip_Flop d_ff_3 (.D(xnor_1_out), .clk(in_52), .Q(out_92), .Qn(d_ff_3_qn));  // open: preset, reset
  J_K_Flip_Flop #(.trigger("falling")) j_k_ff_1 (
    .J(\T_pełny ), .K(\T_pełny ), .clk(in_54), .Q(out_93));  // open: Qn, preset, reset
  J_K_Flip_Flop #(.trigger("falling")) j_k_ff_2 (
    .J(j_k_ff_2_qn), .K(j_k_ff_2_q), .clk(in_55), .Q(j_k_ff_2_q), .Qn(j_k_ff_2_qn));  // open: preset, reset
  nand nand_33 (Q_9, nand_19_out, Q_10);
  nand nand_34 (Q_10, Q_9, nand_20_out);
  not not_4 (not_4_out, CLK_4);
  not not_5 (not_5_out, CLK_5);
  nand nand_35 (Q_21, nand_27_out, Q_23);
  nand nand_36 (Q_23, Q_21, nand_28_out);
  not not_6 (not_6_out, CLK_7);
  nand nand_37 (Q_29, nand_31_out, Q_31);
  nand nand_38 (Q_31, Q_29, nand_32_out);
  D_Flip_Flop #(.trigger("falling")) d_ff_4 (.D(d_ff_1_q), .clk(in_32), .Q(d_ff_4_q));  // open: Qn, preset, reset
  not not_7 (not_7_out, Q_13);
  not not_8 (not_8_out, and_1_out);
  not not_9 (not_9_out, CLK_8);
  D_Flip_Flop #(.trigger("falling")) d_ff_5 (.D(d_ff_4_q), .clk(in_32), .Q(d_ff_5_q));  // open: Qn, preset, reset
  nand nand_39 (nand_39_out, Q_13, not_4_out);
  nand nand_40 (nand_40_out, not_4_out, not_7_out);
  nand nand_41 (nand_41_out, Q_17, ~Q_19, not_5_out);  // NAND_Gate
  nand nand_42 (nand_42_out, not_5_out, ~Q_17, Q_19);  // NAND_Gate
  not not_10 (not_10_out, Q_21);
  nand nand_43 (nand_43_out, Q_25, ~Q_27, not_6_out);  // NAND_Gate
  nand nand_44 (nand_44_out, not_6_out, ~Q_25, Q_27);  // NAND_Gate
  D_Flip_Flop #(.trigger("falling")) d_ff_6 (.D(d_ff_5_q), .clk(in_32), .Q(d_ff_6_q));  // open: Qn, preset, reset
  nand nand_45 (Q_14, nand_39_out, Q_16);
  nand nand_46 (Q_16, Q_14, nand_40_out);
  nand nand_47 (Q_18, nand_41_out, Q_20);
  nand nand_48 (Q_20, Q_18, nand_42_out);
  nand nand_49 (nand_49_out, Q_21, not_8_out);
  nand nand_50 (nand_50_out, not_8_out, not_10_out);
  nand nand_51 (Q_26, nand_43_out, Q_28);
  nand nand_52 (Q_28, Q_26, nand_44_out);
  nand nand_53 (nand_53_out, Q_29, ~Q_31, not_9_out);  // NAND_Gate
  nand nand_54 (nand_54_out, not_9_out, ~Q_29, Q_31);  // NAND_Gate
  nand nand_55 (Q_22, nand_49_out, Q_24);
  nand nand_56 (Q_24, Q_22, nand_50_out);
  nand nand_57 (Q_30, nand_53_out, Q_32);
  nand nand_58 (Q_32, Q_30, nand_54_out);
  // NAND_Gate nand_59 has open pins: in0=S_8, in1=undriven, in2=undriven_2, out=open
  T_Flip_Flop #(.trigger("falling")) t_ff_1 (.T(in_27), .clk(in_29), .Q(out_87));  // open: Qn, reset, preset
  D_Flip_Flop #(.trigger("low")) d_ff_7 (.D(in_36), .clk(in_38), .Q(d_ff_7_q));  // open: Qn, preset, reset
  S_R_Flip_Flop #(.trigger("high")) s_r_ff_3 (
    .S(in_43), .R(in_45), .clk(in_46), .Q(s_r_ff_3_q), .Qn(s_r_ff_3_qn));  // open: reset, preset
  D_Flip_Flop #(.trigger("falling")) d_ff_8 (
    .D(d_ff_8_qn), .clk(and_4_out), .Q(out_91), .Qn(d_ff_8_qn));  // open: preset, reset
  and and_4 (and_4_out, in_50, d_ff_8_qn);
  T_Flip_Flop #(.trigger("falling")) t_ff_2 (.T(out_87), .clk(in_29), .Q(out_86));  // open: Qn, reset, preset
  S_R_Flip_Flop #(.trigger("low")) s_r_ff_4 (
    .S(s_r_ff_3_q), .R(s_r_ff_3_qn), .clk(in_46), .Q(s_r_ff_4_q));  // open: reset, Qn, preset
  D_Flip_Flop #(.trigger("high")) d_ff_9 (.D(in_36), .clk(d_ff_7_q), .Q(d_ff_9_q));  // open: Qn, preset, reset
  T_Flip_Flop t_ff_3 (.clk(in_41), .Q(t_ff_3_q));  // open: T, Qn, reset, preset
  and and_5 (and_5_out, in_37, s_r_ff_5_q);
  S_R_Flip_Flop #(.trigger("falling")) s_r_ff_5 (
    .S(and_6_out), .R(and_5_out), .clk(in_42), .Q(s_r_ff_5_q), .Qn(s_r_ff_5_qn));  // open: reset, preset
  and and_6 (and_6_out, s_r_ff_5_qn, in_44);

  // Notes on the sheet:
  //   Przerzutnik RS
  //   _
  //   _
  //   Dwie jedynki na wejściu - stan oczekiwania
  //   Oszukany RS na NANDach
  //   Synchroniczny RS
  //   Pełne ~T
  //   JK
  //   Stan zabroniony - dwa zera na wyjściu (logika się psuje)
  //   Synchroniczny RS bez stanu zabronionego
  //   Przerzutnik D (aktywowany zboczem)
  //   ~T
  //   T pełny
  //   T uproszczony
  //   _
  //   _
  //   _
  //   _
  //   _
  //   Przerzutnik D (zatrzaskiwany zboczem)
  //   Przerzutnik RS (zatrzaskiwany zboczem)
  //   Przerzutnik T z RS synchronicznego
  //   Przerzutnik JK (zastępuje RS i T, lub też D)
  //   Rejestr przesuwny
  //   _
  //   _
  //   _
  //   Przerzutnik T (niepełny) (dzielnik częstotliwości) (licznik)
  //   _
  //   _
  //   _
  //   _
  //   _
  //   _
  //   _
  //   _
  //   Trzeba na chwilę podłączyć przycisk i poklikać aż będzie zielone
endmodule
