// Logisim project 28052018.circ as structural Verilog: 1 circuit, main circuit main
module main (
  input  CLK,
  input  D0,
  input  D1,
  input  D2,
  input  D3,
  input  in_6,
  input  in_7,
  input  in_8,
  input  in_9,
  input  _1,
  input  _2,
  input  _4,
  input  _8,
  input  in_14,
  input  in_15,
  input  in_16,
  input  in_17,
  input  in_18,
  input  in_19,
  input  in_20,
  input  in_21,
  input  in_22,
  output out_23,
  output out_24,
  output out_25,
  output out_26,
  output out_27,
  output out_28,
  output out_29,
  output out_30,
  output _1_2,
  output _2_2,
  output _4_2,
  output _8_2,
  output _1_3,
  output _2_3,
  output _4_3,
  output _8_3,
  output _1_4,
  output _2_4,
  output _4_4,
  output _8_4,
  output _1_5,
  output _2_5,
  output _4_5
);

  wire and_1_out, and_2_out, and_3_out, and_4_out, and_5_out, nor_1_out, t_ff_4_qn, t_ff_5_qn, t_ff_9_qn,
       t_ff_10_qn, t_ff_13_qn, t_ff_14_qn, t_ff_20_q, xor_1_out, xor_2_out, xor_3_out, xor_4_out;

  T_Flip_Flop #(.trigger("falling")) t_ff_1 (.T(in_6), .clk(in_7), .Q(out_27), .reset(and_3_out));  // open: Qn, preset
  T_Flip_Flop #(.trigger("falling")) t_ff_2 (.T(in_8), .clk(in_9), .Q(_1_2), .reset(nor_1_out));  // open: Qn, preset
  nor nor_1 (nor_1_out, xor_4_out, xor_3_out, xor_2_out, xor_1_out);
  xor xor_1 (xor_1_out, _1_2, _1);
  T_Flip_Flop t_ff_3 (.T(in_14), .clk(in_15), .Q(_1_3));  // open: Qn, reset, preset
  T_Flip_Flop #(.trigger("falling")) t_ff_4 (.T(in_16), .clk(in_17), .Q(_1_4), .Qn(t_ff_4_qn));  // open: reset, preset
  T_Flip_Flop #(.trigger("falling")) t_ff_5 (
    .T(in_18), .clk(in_19), .Q(_1_5), .Qn(t_ff_5_qn), .reset(and_1_out));  // open: preset
  and and_1 (and_1_out, in_20, and_5_out);
  D_Flip_Flop #(.trigger("falling")) d_ff_1 (.D(D0), .clk(CLK), .Q(out_23));  // open: Qn, preset, reset
  D_Flip_Flop #(.trigger("falling")) d_ff_2 (.D(D1), .clk(CLK), .Q(out_24));  // open: Qn, preset, reset
  D_Flip_Flop #(.trigger("falling")) d_ff_3 (.D(D2), .clk(CLK), .Q(out_25));  // open: Qn, preset, reset
  D_Flip_Flop #(.trigger("falling")) d_ff_4 (.D(D3), .clk(CLK), .Q(out_26));  // open: Qn, preset, reset
  T_Flip_Flop #(.trigger("falling")) t_ff_6 (
    .T(in_6), .clk(out_27), .Q(out_28), .reset(and_3_out));  // open: Qn, preset
  T_Flip_Flop #(.trigger("falling")) t_ff_7 (.T(in_8), .clk(_1_2), .Q(_2_2), .reset(nor_1_out));  // open: Qn, preset
  xor xor_2 (xor_2_out, _2_2, _2);
  T_Flip_Flop t_ff_8 (.T(in_14), .clk(_1_3), .Q(_2_3));  // open: Qn, reset, preset
  T_Flip_Flop #(.trigger("falling")) t_ff_9 (
    .T(in_16), .clk(t_ff_4_qn), .Q(_2_4), .Qn(t_ff_9_qn));  // open: reset, preset
  T_Flip_Flop #(.trigger("falling")) t_ff_10 (
    .T(in_18), .clk(t_ff_5_qn), .Q(_2_5), .Qn(t_ff_10_qn), .reset(and_2_out));  // open: preset
  and and_2 (and_2_out, in_21, and_5_out);
  T_Flip_Flop #(.trigger("falling")) t_ff_11 (
    .T(in_6), .clk(out_28), .Q(out_29), .reset(and_3_out));  // open: Qn, preset
  and and_3 (and_3_out, out_29, out_30);
  xor xor_3 (xor_3_out, _4_2, _4);
  T_Flip_Flop t_ff_12 (.T(in_14), .clk(_2_3), .Q(_4_3));  // open: Qn, reset, preset
  T_Flip_Flop #(.trigger("falling")) t_ff_13 (
    .T(in_16), .clk(t_ff_9_qn), .Q(_4_4), .Qn(t_ff_13_qn));  // open: reset, preset
  T_Flip_Flop #(.trigger("falling")) t_ff_14 (
    .T(in_18), .clk(t_ff_10_qn), .Q(_4_5), .Qn(t_ff_14_qn), .reset(and_4_out));  // open: preset
  and and_4 (and_4_out, in_22, and_5_out);
  T_Flip_Flop #(.trigger("falling")) t_ff_15 (.T(in_8), .clk(_2_2), .Q(_4_2), .reset(nor_1_out));  // open: Qn, preset
  T_Flip_Flop #(.trigger("falling")) t_ff_16 (
    .T(in_6), .clk(out_29), .Q(out_30), .reset(and_3_out));  // open: Qn, preset
  T_Flip_Flop #(.trigger("falling")) t_ff_17 (.T(in_8), .clk(_4_2), .Q(_8_2), .reset(nor_1_out));  // open: Qn, preset
  xor xor_4 (xor_4_out, _8_2, _8);
  T_Flip_Flop t_ff_18 (.T(in_14), .clk(_4_3), .Q(_8_3));  // open: Qn, reset, preset
  T_Flip_Flop #(.trigger("falling")) t_ff_19 (.T(in_16), .clk(t_ff_13_qn), .Q(_8_4));  // open: Qn, reset, preset
  T_Flip_Flop #(.trigger("falling")) t_ff_20 (
    .T(in_18), .clk(t_ff_14_qn), .Q(t_ff_20_q), .reset(and_5_out));  // open: Qn, preset
  and and_5 (and_5_out, _1_5, _2_5, _4_5, t_ff_20_q);

  // Notes on the sheet:
  //   4 bitowy rejestr lub zatrzask (latch)
  //   Ustawianie licznika
  //   Przy Rising Edge licznik liczy w dół
  //   Licznik
  //   Licznik który się daje w każdej chwili (10 s pauzy) w każdej chwili ustawić
  //   Liczący w dół, tylko przy falling edge. Sygnał przekazywany z ~Q
  //   Licznik nastawny (programowalny)
  //   Chuj wie czy to działa
  //   Ten ostatni ma raka, bo Kotyra mówi, że tak trzeba
endmodule
